// Logisim project P3Complex.circ as structural Verilog
module GRF (
  input  [4:0] ReadReg1,
  input  reset,
  input  [4:0] WriteReg,
  input  Clk,
  input  WriteEn,
  input  [31:0] WData,
  input  [4:0] ReadReg2,
  output [31:0] RData1,
  output [31:0] RData2
);

  wire [7:0] and_1_out_2, and_1_out_3;
  wire [15:0] and_1_out;
  wire [31:0] _0, _1, _2, _3, _4, _5, _6, _7, _8, _9, _10, _11, _12, _13, _14, _15, _16, _17, _18, _19, _20,
       _21, _22, _23, _24, _25, _26, _27, _28, _29, _30, _31, decoder_1_out0, multiplexer_1_out;

  Decoder #(.select(5), .enable("false")) decoder_1 (
    .out0(decoder_1_out0[0]), .out1(decoder_1_out0[1]), .out2(decoder_1_out0[2]), .out3(decoder_1_out0[3]),
    .out4(decoder_1_out0[4]), .out5(decoder_1_out0[5]), .out6(decoder_1_out0[6]), .out7(decoder_1_out0[7]),
    .out8(decoder_1_out0[8]), .out9(decoder_1_out0[9]), .out10(decoder_1_out0[10]),
    .out11(decoder_1_out0[11]), .out12(decoder_1_out0[12]), .out13(decoder_1_out0[13]),
    .out14(decoder_1_out0[14]), .out15(decoder_1_out0[15]), .out16(decoder_1_out0[16]),
    .out17(decoder_1_out0[17]), .out18(decoder_1_out0[18]), .out19(decoder_1_out0[19]),
    .out20(decoder_1_out0[20]), .out21(decoder_1_out0[21]), .out22(decoder_1_out0[22]),
    .out23(decoder_1_out0[23]), .out24(decoder_1_out0[24]), .out25(decoder_1_out0[25]),
    .out26(decoder_1_out0[26]), .out27(decoder_1_out0[27]), .out28(decoder_1_out0[28]),
    .out29(decoder_1_out0[29]), .out30(decoder_1_out0[30]), .out31(decoder_1_out0[31]), .sel(WriteReg));
  Multiplexer #(.width(32), .enable("false")) multiplexer_1 (
    .in0({32{1'b0}}), .in1({32{1'b1}}), .out(multiplexer_1_out), .sel(WriteEn));
  assign {and_1_out_3, and_1_out_2, and_1_out} = decoder_1_out0 & multiplexer_1_out;  // AND_Gate and_1, 32 bits wide
  Register #(.width(32)) u__0 (.D(WData), .en(1'b0), .Q(_0), .clk(Clk), .clr(reset));
  Register #(.width(32)) u__1 (.D(WData), .en(and_1_out[1]), .Q(_1), .clk(Clk), .clr(reset));
  Register #(.width(32)) u__2 (.D(WData), .en(and_1_out[2]), .Q(_2), .clk(Clk), .clr(reset));
  Register #(.width(32)) u__3 (.D(WData), .en(and_1_out[3]), .Q(_3), .clk(Clk), .clr(reset));
  Register #(.width(32)) u__4 (.D(WData), .en(and_1_out[4]), .Q(_4), .clk(Clk), .clr(reset));
  Register #(.width(32)) u__5 (.D(WData), .en(and_1_out[5]), .Q(_5), .clk(Clk), .clr(reset));
  Register #(.width(32)) u__6 (.D(WData), .en(and_1_out[6]), .Q(_6), .clk(Clk), .clr(reset));
  Register #(.width(32)) u__7 (.D(WData), .en(and_1_out[7]), .Q(_7), .clk(Clk), .clr(reset));
  Register #(.width(32)) u__8 (.D(WData), .en(and_1_out[8]), .Q(_8), .clk(Clk), .clr(reset));
  Register #(.width(32)) u__9 (.D(WData), .en(and_1_out[9]), .Q(_9), .clk(Clk), .clr(reset));
  Register #(.width(32)) u__10 (.D(WData), .en(and_1_out[10]), .Q(_10), .clk(Clk), .clr(reset));
  Register #(.width(32)) u__11 (.D(WData), .en(and_1_out[11]), .Q(_11), .clk(Clk), .clr(reset));
  Register #(.width(32)) u__12 (.D(WData), .en(and_1_out[12]), .Q(_12), .clk(Clk), .clr(reset));
  Register #(.width(32)) u__13 (.D(WData), .en(and_1_out[13]), .Q(_13), .clk(Clk), .clr(reset));
  Register #(.width(32)) u__14 (.D(WData), .en(and_1_out[14]), .Q(_14), .clk(Clk), .clr(reset));
  Register #(.width(32)) u__15 (.D(WData), .en(and_1_out[15]), .Q(_15), .clk(Clk), .clr(reset));
  Register #(.width(32)) u__16 (.D(WData), .en(and_1_out_2[0]), .Q(_16), .clk(Clk), .clr(reset));
  Register #(.width(32)) u__17 (.D(WData), .en(and_1_out_2[1]), .Q(_17), .clk(Clk), .clr(reset));
  Register #(.width(32)) u__18 (.D(WData), .en(and_1_out_2[2]), .Q(_18), .clk(Clk), .clr(reset));
  Register #(.width(32)) u__19 (.D(WData), .en(and_1_out_2[3]), .Q(_19), .clk(Clk), .clr(reset));
  Register #(.width(32)) u__20 (.D(WData), .en(and_1_out_2[4]), .Q(_20), .clk(Clk), .clr(reset));
  Register #(.width(32)) u__21 (.D(WData), .en(and_1_out_2[5]), .Q(_21), .clk(Clk), .clr(reset));
  Register #(.width(32)) u__22 (.D(WData), .en(and_1_out_2[6]), .Q(_22), .clk(Clk), .clr(reset));
  Register #(.width(32)) u__23 (.D(WData), .en(and_1_out_2[7]), .Q(_23), .clk(Clk), .clr(reset));
  Register #(.width(32)) u__24 (.D(WData), .en(and_1_out_3[0]), .Q(_24), .clk(Clk), .clr(reset));
  Register #(.width(32)) u__25 (.D(WData), .en(and_1_out_3[1]), .Q(_25), .clk(Clk), .clr(reset));
  Register #(.width(32)) u__26 (.D(WData), .en(and_1_out_3[2]), .Q(_26), .clk(Clk), .clr(reset));
  Register #(.width(32)) u__27 (.D(WData), .en(and_1_out_3[3]), .Q(_27), .clk(Clk), .clr(reset));
  Register #(.width(32)) u__28 (.D(WData), .en(and_1_out_3[4]), .Q(_28), .clk(Clk), .clr(reset));
  Register #(.width(32)) u__29 (.D(WData), .en(and_1_out_3[5]), .Q(_29), .clk(Clk), .clr(reset));
  Register #(.width(32)) u__30 (.D(WData), .en(and_1_out_3[6]), .Q(_30), .clk(Clk), .clr(reset));
  Register #(.width(32)) u__31 (.D(WData), .en(and_1_out_3[7]), .Q(_31), .clk(Clk), .clr(reset));
  Multiplexer #(.select(5), .width(32), .enable("false")) multiplexer_2 (
    .in0(_0), .in1(_1), .in2(_2), .in3(_3), .in4(_4), .in5(_5), .in6(_6), .in7(_7), .in8(_8), .in9(_9),
    .in10(_10), .in11(_11), .in12(_12), .in13(_13), .in14(_14), .in15(_15), .in16(_16), .in17(_17),
    .in18(_18), .in19(_19), .in20(_20), .in21(_21), .in22(_22), .in23(_23), .in24(_24), .in25(_25),
    .in26(_26), .in27(_27), .in28(_28), .in29(_29), .in30(_30), .in31(_31), .out(RData1), .sel(ReadReg1));
  Multiplexer #(.select(5), .width(32), .enable("false")) multiplexer_3 (
    .in0(_0), .in1(_1), .in2(_2), .in3(_3), .in4(_4), .in5(_5), .in6(_6), .in7(_7), .in8(_8), .in9(_9),
    .in10(_10), .in11(_11), .in12(_12), .in13(_13), .in14(_14), .in15(_15), .in16(_16), .in17(_17),
    .in18(_18), .in19(_19), .in20(_20), .in21(_21), .in22(_22), .in23(_23), .in24(_24), .in25(_25),
    .in26(_26), .in27(_27), .in28(_28), .in29(_29), .in30(_30), .in31(_31), .out(RData2), .sel(ReadReg2));
endmodule

module DataMemory (
  input  MemWrite,
  input  MemRead,
  input  [31:0] Addr,
  input  Clk,
  input  reset,
  input  [31:0] WData,
  output [31:0] Out
);

  wire [4:0] bit_extender_1_out;

  Bit_Extender #(.in_width(32), .out_width(5)) bit_extender_1 (.in(Addr), .out(bit_extender_1_out));
  RAM #(.addrWidth(5), .dataWidth(32), .bus("separate")) ram_1 (
    .addr(bit_extender_1_out), .din(WData), .data(Out), .str(MemWrite), .clk(Clk), .ld(MemRead), .clr(reset));  // open: sel
endmodule

module ALU (
  input  [31:0] A,
  input  [31:0] B,
  input  [1:0] ALUOp,
  output [31:0] Outcome,
  output Zero
);

  wire [31:0] adder_1_out, or_1_out, subtractor_1_out;

  Adder #(.width(32)) adder_1 (.a(A), .b(B), .out(adder_1_out));  // open: cin, cout
  Subtractor #(.width(32)) subtractor_1 (.a(A), .b(B), .out(subtractor_1_out));  // open: bin, bout
  assign or_1_out = A | B;  // OR_Gate or_1, 32 bits wide
  Comparator #(.width(32), .mode("unsigned")) comparator_1 (.a(A), .b(B), .eq(Zero));  // open: gt, lt
  Multiplexer #(.select(2), .width(32), .enable("false")) multiplexer_1 (
    .in0(adder_1_out), .in1(subtractor_1_out), .in2(or_1_out), .out(Outcome), .sel(ALUOp));  // open: in3
endmodule

module Control_Unit (
  input  [5:0] Op,
  input  [5:0] Func,
  output Branch,
  output [1:0] MemtoReg,
  output MemWrite,
  output MemRead,
  output [1:0] ALUOp,
  output ALUSrc,
  output RegWrite,
  output WriteRegDist,
  output Jump
);

  wire addu, And, Bgez, Blez, J, Jal, Jalr, Jr, not_1_out, not_2_out, not_3_out, not_4_out, not_5_out,
       not_6_out, not_7_out, not_8_out, not_9_out, not_10_out, not_11_out, not_12_out, sll, Slt, Srl;

  not not_1 (not_1_out, Op[4]);
  not not_2 (not_2_out, Op[5]);
  not not_3 (not_3_out, Op[2]);
  not not_4 (not_4_out, Op[3]);
  not not_5 (not_5_out, Op[0]);
  not not_6 (not_6_out, Op[1]);
  not not_7 (not_7_out, Func[5]);
  not not_8 (not_8_out, Func[4]);
  not not_9 (not_9_out, Func[3]);
  not not_10 (not_10_out, Func[2]);
  not not_11 (not_11_out, Func[1]);
  not not_12 (not_12_out, Func[0]);
  and u_addu (addu, Func[5], not_8_out, not_9_out, not_10_out, not_11_out, Func[0], not_5_out, not_6_out, not_3_out, not_4_out, not_1_out, not_2_out);
  and subu (ALUOp[0], Func[5], not_8_out, not_9_out, not_10_out, Func[1], Func[0], not_5_out, not_6_out, not_3_out, not_4_out, not_1_out, not_2_out);
  and u_sll (sll, not_12_out, not_11_out, not_10_out, not_9_out, not_8_out, not_7_out, not_5_out, not_6_out, not_3_out, not_4_out, not_1_out, not_2_out);
  and ori (ALUOp[1], not_2_out, not_1_out, Op[3], Op[2], not_6_out, Op[0]);
  and lw (MemRead, Op[5], not_1_out, not_4_out, not_3_out, Op[1], Op[0]);
  and sw (MemWrite, Op[5], not_1_out, Op[3], not_3_out, Op[1], Op[0]);
  and lui (MemtoReg[1], not_2_out, not_1_out, Op[3], Op[2], Op[1], Op[0]);
  and beq (Branch, not_2_out, not_1_out, not_4_out, Op[2], not_6_out, not_5_out);
  and u_J (J, not_2_out, not_1_out, not_4_out, not_3_out, Op[1], not_5_out);
  and u_Jal (Jal, not_2_out, not_1_out, not_4_out, not_3_out, Op[1], Op[0]);
  and u_Jalr (Jalr, not_2_out, not_1_out, not_4_out, not_3_out, not_6_out, not_5_out, not_7_out, not_8_out, Func[3], not_10_out, not_11_out, Func[0]);
  and u_Jr (Jr, not_2_out, not_1_out, not_4_out, not_3_out, not_6_out, not_5_out, not_7_out, not_8_out, Func[3], not_10_out, not_11_out, not_12_out);
  and u_Slt (Slt, not_2_out, not_1_out, not_4_out, not_3_out, not_6_out, not_5_out, Func[5], not_8_out, Func[3], not_10_out, Func[1], not_12_out);
  and u_And (And, not_2_out, not_1_out, not_4_out, not_3_out, not_6_out, not_5_out, Func[5], not_8_out, not_9_out, Func[2], not_11_out, not_12_out);
  and u_Srl (Srl, not_2_out, not_1_out, not_4_out, not_3_out, not_6_out, not_5_out, not_7_out, not_8_out, not_9_out, not_10_out, Func[1], not_12_out);
  and u_Bgez (Bgez, not_2_out, not_1_out, not_4_out, not_3_out, not_6_out, Op[0]);
  and u_Blez (Blez, not_2_out, not_1_out, not_4_out, Op[2], Op[1], not_5_out);
  or or_1 (ALUSrc, ALUOp[1], MemRead, MemWrite);
  or or_2 (RegWrite, addu, ALUOp[0], ALUOp[1], MemRead, MemtoReg[1]);
  or or_3 (WriteRegDist, addu, ALUOp[0]);
  or or_4 (Jump, J, Jal);

  assign MemtoReg[0] = MemRead;

  // Other names for the same wires on the sheet: subu = ALUOp[0]; ori = ALUOp[1]; beq = Branch; lw = MemRead;
  //   lui = MemtoReg[1]; sw = MemWrite
endmodule

module IFU (
  input  [31:0] PC_Update,
  input  Clk,
  input  Reset,
  output [31:0] PC_current,
  output [31:0] Instruction
);

  Register #(.width(32)) PC (.D(PC_Update), .Q(PC_current), .clk(Clk), .clr(Reset));  // open: en
  ROM #(.addrWidth(5), .dataWidth(32)) rom_1 (.addr(PC_current[6:2]), .data(Instruction));  // open: sel

  // Notes on the sheet:
  //   contents of rom_1 (hex, n*v repeats v):
  //   0 3c080001 35080001 1084821 1284823 0 0 0 11290000 ac090000 8c0a0000 1000ffff
endmodule
