// Logisim project PerCycleCPU.circ as structural Verilog: 7 circuits, main circuit main
module main (
  input  Reset
);

  wire alu_1_zero, and_1_out, control_unit_1_alusrc, control_unit_1_branch, control_unit_1_memread,
       control_unit_1_memwrite, control_unit_1_regwrite, control_unit_1_writeregdist;
  wire [1:0] control_unit_1_aluop, control_unit_1_memtoreg;
  wire [3:0] alucontrol_1_aluoperation;
  wire [4:0] multiplexer_1_out;
  wire [31:0] adder_1_out, adder_2_out, alu_1_outcome, datamemory_1_out, grf_1_rdata1, grf_1_rdata2,
       ifu_1_instruction, ifu_1_pc_current, multiplexer_2_out, multiplexer_3_out, multiplexer_4_out,
       multiplier_1_out, sign_ext;

  IFU ifu_1 (
    .PC_Update(multiplexer_3_out), .Reset(Reset), .Instruction(ifu_1_instruction),
    .PC_current(ifu_1_pc_current));
  Adder #(.width(32)) adder_1 (.a(32'h4), .b(ifu_1_pc_current), .out(adder_1_out));  // open: cin, cout
  Multiplier #(.width(32)) multiplier_1 (.a(sign_ext), .b(32'h4), .out(multiplier_1_out));  // open: cin, cout
  Multiplexer #(.width(5), .enable("false")) multiplexer_1 (
    .in0(ifu_1_instruction[20:16]), .in1(ifu_1_instruction[15:11]), .out(multiplexer_1_out),
    .sel(control_unit_1_writeregdist));
  assign sign_ext = {{16{1'b0}}, ifu_1_instruction[15:0]};  // Bit_Extender bit_extender_1
  Control_Unit control_unit_1 (
    .Op(ifu_1_instruction[31:26]), .WriteRegDist(control_unit_1_writeregdist),
    .Branch(control_unit_1_branch), .MemtoReg(control_unit_1_memtoreg), .MemWrite(control_unit_1_memwrite),
    .MemRead(control_unit_1_memread), .ALUOp(control_unit_1_aluop), .ALUSrc(control_unit_1_alusrc),
    .RegWrite(control_unit_1_regwrite));
  Adder #(.width(32)) adder_2 (.a(adder_1_out), .b(multiplier_1_out), .out(adder_2_out));  // open: cin, cout
  GRF grf_1 (
    .ReadReg1(ifu_1_instruction[25:21]), .WriteReg(multiplexer_1_out), .WriteEn(control_unit_1_regwrite),
    .WriteData(multiplexer_4_out), .RData1(grf_1_rdata1), .RData2(grf_1_rdata2),
    .ReadReg2(ifu_1_instruction[20:16]));
  Multiplexer #(.width(32), .enable("false")) multiplexer_2 (
    .in0(grf_1_rdata2), .in1(sign_ext), .out(multiplexer_2_out), .sel(control_unit_1_alusrc));
  Multiplexer #(.width(32), .enable("false")) multiplexer_3 (
    .in0(adder_1_out), .in1(adder_2_out), .out(multiplexer_3_out), .sel(and_1_out));
  and and_1 (and_1_out, control_unit_1_branch, alu_1_zero);
  ALUControl alucontrol_1 (
    .ALUOp(control_unit_1_aluop), .Func(ifu_1_instruction[5:0]), .ALUOperation(alucontrol_1_aluoperation));
  ALU alu_1 (
    .A(grf_1_rdata1), .B(multiplexer_2_out), .ALUOp(alucontrol_1_aluoperation), .Zero(alu_1_zero),
    .Outcome(alu_1_outcome));
  DataMemory datamemory_1 (
    .Addr(alu_1_outcome), .WData(grf_1_rdata2), .Out(datamemory_1_out), .MemWrite(control_unit_1_memwrite),
    .MemRead(control_unit_1_memread));
  Multiplexer #(.select(2), .width(32), .enable("false")) multiplexer_4 (
    .in0(alu_1_outcome), .in1(datamemory_1_out), .in2(sign_ext), .out(multiplexer_4_out),
    .sel(control_unit_1_memtoreg));  // open: in3

  // Notes on the sheet:
  //   IFU
  //   GRF
  //   ALU
  //   DM
endmodule

module GRF (
  input  [4:0] ReadReg1,
  input  [4:0] WriteReg,
  input  WriteEn,
  input  [31:0] WriteData,
  input  [4:0] ReadReg2,
  output [31:0] RData1,
  output [31:0] RData2
);

  wire Clk_out;
  wire [7:0] and_1_out_2;
  wire [23:0] and_1_out;
  wire [31:0] _0, _1, _2, _3, _4, _5, _6, _7, _8, _9, _10, _11, _12, _13, _14, _15, _16, _17, _18, _19, _20,
       _21, _22, _23, _24, _25, _26, _27, _28, _29, _30, _31, decoder_1_out0, multiplexer_1_out,
       multiplexer_2_out;

  Clock Clk (.out(Clk_out));
  Decoder #(.select(5), .enable("false")) decoder_1 (
    .out0(decoder_1_out0[0]), .out1(decoder_1_out0[1]), .out2(decoder_1_out0[2]), .out3(decoder_1_out0[3]),
    .out4(decoder_1_out0[4]), .out5(decoder_1_out0[5]), .out6(decoder_1_out0[6]), .out7(decoder_1_out0[7]),
    .out8(decoder_1_out0[8]), .out9(decoder_1_out0[9]), .out10(decoder_1_out0[10]),
    .out11(decoder_1_out0[11]), .out12(decoder_1_out0[12]), .out13(decoder_1_out0[13]),
    .out14(decoder_1_out0[14]), .out15(decoder_1_out0[15]), .out16(decoder_1_out0[16]),
    .out17(decoder_1_out0[17]), .out18(decoder_1_out0[18]), .out19(decoder_1_out0[19]),
    .out20(decoder_1_out0[20]), .out21(decoder_1_out0[21]), .out22(decoder_1_out0[22]),
    .out23(decoder_1_out0[23]), .out24(decoder_1_out0[24]), .out25(decoder_1_out0[25]),
    .out26(decoder_1_out0[26]), .out27(decoder_1_out0[27]), .out28(decoder_1_out0[28]),
    .out29(decoder_1_out0[29]), .out30(decoder_1_out0[30]), .out31(decoder_1_out0[31]), .sel(WriteReg));
  Multiplexer #(.width(32), .enable("false")) multiplexer_1 (
    .in0({32{1'b0}}), .in1({32{1'b1}}), .out(multiplexer_1_out), .sel(Clk_out));
  Multiplexer #(.width(32), .enable("false")) multiplexer_2 (
    .in0({32{1'b0}}), .in1({32{1'b1}}), .out(multiplexer_2_out), .sel(WriteEn));
  assign {and_1_out_2, and_1_out} = decoder_1_out0 & multiplexer_1_out & multiplexer_2_out;  // AND_Gate and_1, 32 bits wide
  Register #(.width(32)) u__0 (.D(WriteData), .en(1'b0), .Q(_0), .clk(and_1_out[0]));  // open: clr
  Register #(.width(32)) u__1 (.D(WriteData), .Q(_1), .clk(and_1_out[1]));  // open: en, clr
  Register #(.width(32)) u__2 (.D(WriteData), .Q(_2), .clk(and_1_out[2]));  // open: en, clr
  Register #(.width(32)) u__3 (.D(WriteData), .Q(_3), .clk(and_1_out[3]));  // open: en, clr
  Register #(.width(32)) u__4 (.D(WriteData), .Q(_4), .clk(and_1_out[4]));  // open: en, clr
  Register #(.width(32)) u__5 (.D(WriteData), .Q(_5), .clk(and_1_out[5]));  // open: en, clr
  Register #(.width(32)) u__6 (.D(WriteData), .Q(_6), .clk(and_1_out[6]));  // open: en, clr
  Register #(.width(32)) u__7 (.D(WriteData), .Q(_7), .clk(and_1_out[7]));  // open: en, clr
  Register #(.width(32)) u__8 (.D(WriteData), .Q(_8), .clk(and_1_out[8]));  // open: en, clr
  Register #(.width(32)) u__9 (.D(WriteData), .Q(_9), .clk(and_1_out[9]));  // open: en, clr
  Register #(.width(32)) u__10 (.D(WriteData), .Q(_10), .clk(and_1_out[10]));  // open: en, clr
  Register #(.width(32)) u__11 (.D(WriteData), .Q(_11), .clk(and_1_out[11]));  // open: en, clr
  Register #(.width(32)) u__12 (.D(WriteData), .Q(_12), .clk(and_1_out[12]));  // open: en, clr
  Register #(.width(32)) u__13 (.D(WriteData), .Q(_13), .clk(and_1_out[13]));  // open: en, clr
  Register #(.width(32)) u__14 (.D(WriteData), .Q(_14), .clk(and_1_out[14]));  // open: en, clr
  Register #(.width(32)) u__15 (.D(WriteData), .Q(_15), .clk(and_1_out[15]));  // open: en, clr
  Register #(.width(32)) u__16 (.D(WriteData), .Q(_16), .clk(and_1_out[16]));  // open: en, clr
  Register #(.width(32)) u__17 (.D(WriteData), .Q(_17), .clk(and_1_out[17]));  // open: en, clr
  Register #(.width(32)) u__18 (.D(WriteData), .Q(_18), .clk(and_1_out[18]));  // open: en, clr
  Register #(.width(32)) u__19 (.D(WriteData), .Q(_19), .clk(and_1_out[19]));  // open: en, clr
  Register #(.width(32)) u__20 (.D(WriteData), .Q(_20), .clk(and_1_out[20]));  // open: en, clr
  Register #(.width(32)) u__21 (.D(WriteData), .Q(_21), .clk(and_1_out[21]));  // open: en, clr
  Register #(.width(32)) u__22 (.D(WriteData), .Q(_22), .clk(and_1_out[22]));  // open: en, clr
  Register #(.width(32)) u__23 (.D(WriteData), .Q(_23), .clk(and_1_out[23]));  // open: en, clr
  Register #(.width(32)) u__24 (.D(WriteData), .Q(_24), .clk(and_1_out_2[0]));  // open: en, clr
  Register #(.width(32)) u__25 (.D(WriteData), .Q(_25), .clk(and_1_out_2[1]));  // open: en, clr
  Register #(.width(32)) u__26 (.D(WriteData), .Q(_26), .clk(and_1_out_2[2]));  // open: en, clr
  Register #(.width(32)) u__27 (.D(WriteData), .Q(_27), .clk(and_1_out_2[3]));  // open: en, clr
  Register #(.width(32)) u__28 (.D(WriteData), .Q(_28), .clk(and_1_out_2[4]));  // open: en, clr
  Register #(.width(32)) u__29 (.D(WriteData), .Q(_29), .clk(and_1_out_2[5]));  // open: en, clr
  Register #(.width(32)) u__30 (.D(WriteData), .Q(_30), .clk(and_1_out_2[6]));  // open: en, clr
  Register #(.width(32)) u__31 (.D(WriteData), .Q(_31), .clk(and_1_out_2[7]));  // open: en, clr
  Multiplexer #(.select(5), .width(32), .enable("false")) multiplexer_3 (
    .in0(_0), .in1(_1), .in2(_2), .in3(_3), .in4(_4), .in5(_5), .in6(_6), .in7(_7), .in8(_8), .in9(_9),
    .in10(_10), .in11(_11), .in12(_12), .in13(_13), .in14(_14), .in15(_15), .in16(_16), .in17(_17),
    .in18(_18), .in19(_19), .in20(_20), .in21(_21), .in22(_22), .in23(_23), .in24(_24), .in25(_25),
    .in26(_26), .in27(_27), .in28(_28), .in29(_29), .in30(_30), .in31(_31), .out(RData1), .sel(ReadReg1));
  Multiplexer #(.select(5), .width(32), .enable("false")) multiplexer_4 (
    .in0(_0), .in1(_1), .in2(_2), .in3(_3), .in4(_4), .in5(_5), .in6(_6), .in7(_7), .in8(_8), .in9(_9),
    .in10(_10), .in11(_11), .in12(_12), .in13(_13), .in14(_14), .in15(_15), .in16(_16), .in17(_17),
    .in18(_18), .in19(_19), .in20(_20), .in21(_21), .in22(_22), .in23(_23), .in24(_24), .in25(_25),
    .in26(_26), .in27(_27), .in28(_28), .in29(_29), .in30(_30), .in31(_31), .out(RData2), .sel(ReadReg2));

  // Other names for the same wires on the sheet: WData[31:0] = WriteData
endmodule

module DataMemory (
  input  MemWrite,
  input  MemRead,
  input  [31:0] Addr,
  input  [31:0] WData,
  output [31:0] Out
);

  wire clock_1_out;
  wire [4:0] bit_extender_1_out;

  Bit_Extender #(.in_width(32), .out_width(5)) bit_extender_1 (.in(Addr), .out(bit_extender_1_out));
  RAM #(.addrWidth(5), .dataWidth(32), .bus("separate")) ram_1 (
    .addr(bit_extender_1_out), .din(WData), .data(Out), .str(MemWrite), .clk(clock_1_out), .ld(MemRead));  // open: sel, clr
  Clock clock_1 (.out(clock_1_out));
endmodule

module ALU (
  input  [31:0] A,
  input  [31:0] B,
  input  [3:0] ALUOp,
  output [31:0] Outcome,
  output Zero
);

  wire [31:0] adder_1_out, or_1_out, subtractor_1_out;

  Adder #(.width(32)) adder_1 (.a(A), .b(B), .out(adder_1_out));  // open: cin, cout
  Subtractor #(.width(32)) subtractor_1 (.a(A), .b(B), .out(subtractor_1_out));  // open: bin, bout
  assign or_1_out = A | B;  // OR_Gate or_1, 32 bits wide
  Comparator #(.width(32)) comparator_1 (.a(A), .b(B), .eq(Zero));  // open: gt, lt
  Multiplexer #(.select(4), .width(32), .enable("false")) multiplexer_1 (
    .out(Outcome), .sel(ALUOp));  // open: in0, in1, in2, in3, in4, in5, in6, in7, in8, in9, in10, in11, in12, in13, in14, in15
endmodule

module Control_Unit (
  input  [5:0] Op,
  output Branch,
  output [1:0] MemtoReg,
  output MemWrite,
  output MemRead,
  output [1:0] ALUOp,
  output ALUSrc,
  output WriteRegDist,
  output RegWrite
);
endmodule

module IFU (
  input  [31:0] PC_Update,
  input  Reset,
  output [31:0] PC_current,
  output [31:0] Instruction
);

  wire clock_1_out;

  Clock clock_1 (.out(clock_1_out));
  Register #(.width(32)) PC (.D(PC_Update), .Q(PC_current), .clk(clock_1_out), .clr(Reset));  // open: en
  ROM #(.addrWidth(5), .dataWidth(32)) rom_1 (.addr(PC_current[6:2]), .data(Instruction));  // open: sel
endmodule

module ALUControl (
  input  [1:0] ALUOp,
  input  [5:0] Func,
  output [3:0] ALUOperation
);
endmodule
