// Logisim project comparator.circ as structural Verilog
module _1_bit_comparator (
  input  A,
  input  B,
  output C,
  output E
);

  wire and_2_out, and_3_out, not_1_out, not_2_out, not_3_out;

  not not_1 (not_1_out, B);
  not not_2 (not_2_out, A);
  not not_3 (not_3_out, B);
  and and_1 (C, A, not_1_out);
  and and_2 (and_2_out, A, B);
  and and_3 (and_3_out, not_2_out, not_3_out);
  or or_1 (E, and_2_out, and_3_out);
endmodule

module _2_bit_comparator (
  input  [1:0] A,
  input  [1:0] B,
  output C,
  output E
);

  wire multiplexer_1_out, n1_bit_comparator_1_c, n1_bit_comparator_1_e, n1_bit_comparator_2_c,
       n1_bit_comparator_2_e;

  _1_bit_comparator u_1_bit_comparator_1 (.A(A[0]), .B(B[0]), .C(n1_bit_comparator_1_c), .E(n1_bit_comparator_1_e));
  _1_bit_comparator u_1_bit_comparator_2 (.A(A[1]), .B(B[1]), .C(n1_bit_comparator_2_c), .E(n1_bit_comparator_2_e));
  Multiplexer #(.enable("false")) multiplexer_1 (
    .in0(1'b0), .in1(n1_bit_comparator_1_c), .out(multiplexer_1_out), .sel(n1_bit_comparator_2_e));
  or or_1 (C, multiplexer_1_out, n1_bit_comparator_2_c);
  and and_1 (E, n1_bit_comparator_1_e, n1_bit_comparator_2_e);
endmodule

module comparator (
  input  [3:0] A,
  input  [3:0] B,
  output C
);

  wire multiplexer_1_out, n2_bit_comparator_1_c, n2_bit_comparator_2_c, n2_bit_comparator_2_e, or_1_out;

  _2_bit_comparator u_2_bit_comparator_1 (.A(A[1:0]), .B(B[1:0]), .C(n2_bit_comparator_1_c));  // open: E
  _2_bit_comparator u_2_bit_comparator_2 (.A(A[3:2]), .B(B[3:2]), .C(n2_bit_comparator_2_c), .E(n2_bit_comparator_2_e));
  Multiplexer #(.enable("false")) multiplexer_1 (
    .in0(1'b0), .in1(n2_bit_comparator_1_c), .out(multiplexer_1_out), .sel(n2_bit_comparator_2_e));
  or or_1 (or_1_out, multiplexer_1_out, n2_bit_comparator_2_c);
  Multiplexer #(.select(2), .enable("false")) multiplexer_2 (
    .in0(or_1_out), .in1(1'b1), .in2(1'b0), .in3(or_1_out), .out(C), .sel({A[3], B[3]}));
endmodule
